// Logisim project project.circ as structural Verilog: 1 circuit, main circuit main
module main (
  input  Armed,
  input  Door,
  input  Motion,
  input  Forced,
  input  Heat,
  output out_6,
  output Warning,
  output Emergency,
  output Safe,
  output out_10
);

  wire and_1_out, not_1_out, or_1_out, or_2_out, or_3_out;

  and and_1 (and_1_out, Door, Motion);
  or or_1 (or_1_out, Door, Motion, Forced);
  or or_2 (or_2_out, and_1_out, Forced);
  not not_1 (not_1_out, out_6);
  and and_2 (Warning, Armed, or_1_out, not_1_out);
  and and_3 (out_6, Armed, or_2_out);
  or or_3 (or_3_out, Warning, out_6, Heat);
  or or_4 (out_10, out_6, Heat);
  not not_2 (Safe, or_3_out);

  assign Emergency = Heat;

  // Notes on the sheet:
  //   Final Alarm
  //   Intrution
endmodule
